# Fritzing sketch mainboard (saved by Fritzing 0.9.3b)
circuit board: 13cm x 10cm
breadboards: 1

parts:
  Nano = Arduino Nano (Rev3.0)
  Q1 = PNP-Transistor [package="TO92 [THT]"]
  1000C = mystery part, 8 pins [chip_label=?]
  Q2 = PNP-Transistor [package="TO92 [THT]"]
  Q3 = NPN-Transistor [package="TO92 [THT]"]
  Q4 = NPN-Transistor [package="TO92 [THT]"]
  D1 = Rectifier Diode [part_number=1N4001 package="300 mil [THT]"]
  D2 = Rectifier Diode [part_number=1N4001 package="300 mil [THT]"]
  D3 = Rectifier Diode [part_number=1N4001 package="300 mil [THT]"]
  D4 = Rectifier Diode [part_number=1N4001 package="300 mil [THT]"]
  R1 = Resistor [tolerance=±5% resistance=10k package=THT]
  R3 = Resistor [tolerance=±5% resistance=10k package=THT]
  R4 = Resistor [tolerance=±5% resistance=10k package=THT]
  R2 = Resistor [tolerance=±5% resistance=10k package=THT]
  J1 = female pin header, 2 pins [form="♀ (female)"]
  Q5 = PNP-Transistor [package="TO92 [THT]"]
  Q6 = PNP-Transistor [package="TO92 [THT]"]
  Q7 = NPN-Transistor [package="TO92 [THT]"]
  Q8 = NPN-Transistor [package="TO92 [THT]"]
  D8 = Rectifier Diode [part_number=1N4001 package="300 mil [THT]"]
  D6 = Rectifier Diode [part_number=1N4001 package="300 mil [THT]"]
  D5 = Rectifier Diode [part_number=1N4001 package="300 mil [THT]"]
  D7 = Rectifier Diode [part_number=1N4001 package="300 mil [THT]"]
  R8 = Resistor [tolerance=±5% resistance=10k package=THT]
  R6 = Resistor [tolerance=±5% resistance=10k package=THT]
  R7 = Resistor [tolerance=±5% resistance=10k package=THT]
  R5 = Resistor [tolerance=±5% resistance=10k package=THT]
  J2 = female pin header, 2 pins [form="♀ (female)"]
  Raspberry_Pi_Zero = Raspberry Pi 3 [part_number=RPI-3-V1.2]
  Shutdown = Pushbutton [package="[THT]"]
  Power = Toggle Switch [package=THT]
  MinUMU9v5 = mystery part, 5 pins [chip_label=?]
  J3 = female pin header, 3 pins [form="♀ (female)"]
  J4 = female pin header, 3 pins [form="♀ (female)"]
  C1 = Electrolytic Capacitor [capacitance=1µF package="100 mil [THT, electrolytic]"]
  C2 = Ceramic Capacitor [capacitance=100nF package="100 mil [THT, multilayer]"]
  C3 = Ceramic Capacitor [capacitance=100nF package="100 mil [THT, multilayer]"]
  C4 = Ceramic Capacitor [capacitance=100nF package="100 mil [THT, multilayer]"]

nets:
  N1: Nano.D2, J4.pin3
  N2: Nano.D3, J3.pin3
  N3: Nano.D5, R4.Pin_0, R2.Pin_1
  N4: Nano.D6, R1.Pin_1, R3.Pin_0
  N5: Nano.D9, R7.Pin_0, R5.Pin_1
  N6: Nano.D10, R8.Pin_0, R6.Pin_1
  VIN: Nano.VIN, Q1.E, 1000C.pin8, Q2.E, D1.cathode, D2.cathode, Q5.E, Q6.E, D6.cathode, D5.cathode, Raspberry_Pi_Zero.5V, J3.pin2, J4.pin2, C1.+, C2.0, C3.1, C4.1
  N7: Nano.GND, Q3.E, Q4.E, D3.anode, D4.anode, Q7.E, Q8.E, D8.anode, D7.anode, MinUMU9v5.pin3, J3.pin1, J4.pin1, C4.0
  N8: Nano.A5, Raspberry_Pi_Zero.GPIO3, MinUMU9v5.pin1
  N9: Nano.A4, Raspberry_Pi_Zero.GPIO2, MinUMU9v5.pin2
  N10: Q1.B, R1.Pin_0
  N11: Q1.C, Q3.C, D1.anode, D3.cathode, J1.pin2
  N12: 1000C.pin4, Power.COM
  N13: 1000C.pin5, Power.L1
  N14: 1000C.pin7, Raspberry_Pi_Zero.GND, Raspberry_Pi_Zero.GPIO20, Shutdown.Pin_1, Shutdown.Pin_2, Shutdown.Pin_3, Shutdown.Pin_4, C1.-, C2.1, C3.0
  N15: Q2.B, R2.Pin_0
  N16: Q2.C, Q4.C, D2.anode, D4.cathode, J1.pin1
  N17: Q3.B, R3.Pin_1
  N18: Q4.B, R4.Pin_1
  N19: Q5.B, R5.Pin_0
  N20: Q5.C, Q7.C, D5.anode, D7.cathode, J2.pin2
  N21: Q6.B, R6.Pin_0
  N22: Q6.C, Q8.C, D8.cathode, D6.anode, J2.pin1
  N23: Q7.B, R7.Pin_1
  N24: Q8.B, R8.Pin_1
  3V3: Raspberry_Pi_Zero.3v3, Raspberry_Pi_Zero.3V3, MinUMU9v5.pin5
